// Logisim project jesusmultiplicouAMEM.circ as structural Verilog: 1 circuit, main circuit main
module main (
  input  [7:0] A,
  input  RESET,
  input  [7:0] B
);

  wire Clock_out, comparator_1_lt, or_1_out;
  wire [7:0] Contador_q;
  wire [15:0] adder_1_out, Registrador_q;

  Adder #(.width(16)) adder_1 (.a({{8{1'b0}}, A}), .b(Registrador_q), .out(adder_1_out));  // open: cin, cout
  // Probe on Registrador_q
  Register #(.width(16)) Registrador (.D(adder_1_out), .en(or_1_out), .Q(Registrador_q), .clk(Clock_out), .clr(RESET));
  Clock Clock (.out(Clock_out));
  Counter #(.ongoal("stay")) Contador (.Q(Contador_q), .clk(Clock_out), .clr(RESET));  // open: load, D, count, carry
  // Probe on Contador_q
  Comparator #(.mode("unsigned")) comparator_1 (.a(Contador_q), .b(B), .lt(comparator_1_lt));  // open: gt, eq
  or or_1 (or_1_out, comparator_1_lt, comparator_1_lt);
endmodule
