// Logisim project labsd].circ as structural Verilog
module E (
  input  in_1,
  input  in_2,
  output out_3
);

  wire nand_1_out;

  nand nand_1 (nand_1_out, in_1, in_2);
  NAO nao_1 (.in_1(nand_1_out), .out_2(out_3));
endmodule

// ~
module NAO (
  input  in_1,
  output out_2
);

  nand nand_1 (out_2, in_1, in_1);
endmodule

module OU (
  input  in_1,
  input  in_2,
  output out_3
);

  wire nao_1_out_2, nao_2_out_2;

  NAO nao_1 (.in_1(in_1), .out_2(nao_1_out_2));
  NAO nao_2 (.in_1(in_2), .out_2(nao_2_out_2));
  nand nand_1 (out_3, nao_1_out_2, nao_2_out_2);
endmodule

module _1 (
  input  in_1,
  input  in_2,
  input  in_3,
  output out_4
);

  wire e_1_out_3, nao_1_out_2, nao_2_out_2, nao_3_out_2;

  NAO nao_1 (.in_1(in_1), .out_2(nao_1_out_2));
  NAO nao_2 (.in_1(in_2), .out_2(nao_2_out_2));
  NAO nao_3 (.in_1(in_3), .out_2(nao_3_out_2));
  E e_1 (.in_1(nao_1_out_2), .in_2(nao_2_out_2), .out_3(e_1_out_3));
  E e_2 (.in_1(e_1_out_3), .in_2(nao_3_out_2), .out_3(out_4));
endmodule

module _2 (
  input  A,
  input  B,
  input  C,
  output out_4
);

  wire e_1_out_3, nao_1_out_2, nao_2_out_2;

  NAO nao_1 (.in_1(A), .out_2(nao_1_out_2));
  NAO nao_2 (.in_1(B), .out_2(nao_2_out_2));
  E e_1 (.in_1(nao_1_out_2), .in_2(nao_2_out_2), .out_3(e_1_out_3));
  E e_2 (.in_1(e_1_out_3), .in_2(C), .out_3(out_4));
endmodule

module _3 (
  input  A,
  input  B,
  input  C,
  output out_4
);

  wire e_1_out_3, nao_2_out_2, nao_out_2;

  NAO nao (.in_1(A), .out_2(nao_out_2));
  NAO nao_2 (.in_1(C), .out_2(nao_2_out_2));
  E e_1 (.in_1(nao_out_2), .in_2(B), .out_3(e_1_out_3));
  E e_2 (.in_1(e_1_out_3), .in_2(nao_2_out_2), .out_3(out_4));
endmodule

module _4 (
  input  in_1,
  input  in_2,
  input  in_3,
  output out_4
);

  wire e_1_out_3, nao_out_2;

  NAO nao (.in_1(in_1), .out_2(nao_out_2));
  E e_1 (.in_1(nao_out_2), .in_2(in_2), .out_3(e_1_out_3));
  E e_2 (.in_1(e_1_out_3), .in_2(in_3), .out_3(out_4));
endmodule

module _5 (
  input  in_1,
  input  in_2,
  input  in_3,
  output out_4
);

  wire e_1_out_3, nao_2_out_2, nao_out_2;

  NAO nao (.in_1(in_2), .out_2(nao_out_2));
  NAO nao_2 (.in_1(in_3), .out_2(nao_2_out_2));
  E e_1 (.in_1(in_1), .in_2(nao_out_2), .out_3(e_1_out_3));
  E e_2 (.in_1(e_1_out_3), .in_2(nao_2_out_2), .out_3(out_4));
endmodule

module _6 (
  input  in_1,
  input  in_2,
  input  in_3,
  output out_4
);

  wire e_1_out_3, nao_out_2;

  NAO nao (.in_1(in_2), .out_2(nao_out_2));
  E e_1 (.in_1(in_1), .in_2(nao_out_2), .out_3(e_1_out_3));
  E e_2 (.in_1(e_1_out_3), .in_2(in_3), .out_3(out_4));
endmodule

module _7 (
  input  in_1,
  input  in_2,
  input  in_3,
  output out_4
);

  wire e_1_out_3, nao_out_2;

  NAO nao (.in_1(in_3), .out_2(nao_out_2));
  E e_1 (.in_1(in_2), .in_2(nao_out_2), .out_3(e_1_out_3));
  E e_2 (.in_1(in_1), .in_2(e_1_out_3), .out_3(out_4));
endmodule

module ALLL (
  output out_1
);

  wire n1_1_out_4, n2_1_out_4, n3_1_out_4, n4_1_out_4, n5_1_out_4, n6_1_out_4, n7_1_out_4;

  _1 u_1_1 (.out_4(n1_1_out_4));  // open: in_1, in_2, in_3
  _2 u_2_1 (.out_4(n2_1_out_4));  // open: A, B, C
  _3 u_3_1 (.out_4(n3_1_out_4));  // open: A, B, C
  _4 u_4_1 (.out_4(n4_1_out_4));  // open: in_1, in_2, in_3
  _5 u_5_1 (.out_4(n5_1_out_4));  // open: in_1, in_2, in_3
  _6 u_6_1 (.out_4(n6_1_out_4));  // open: in_1, in_2, in_3
  _7 u_7_1 (.out_4(n7_1_out_4));  // open: in_1, in_2, in_3
  OU_7 ou_7_1 (
    .in_1(n1_1_out_4), .in_2(n2_1_out_4), .in_3(n3_1_out_4), .in_4(n4_1_out_4), .in_5(n5_1_out_4),
    .in_6(n6_1_out_4), .in_7(n7_1_out_4), .out_8(out_1));
endmodule

module OU_7 (
  input  in_1,
  input  in_2,
  input  in_3,
  input  in_4,
  input  in_5,
  input  in_6,
  input  in_7,
  output out_8
);

  wire ou_1_out_3, ou_2_out_3, ou_3_out_3, ou_4_out_3, ou_5_out_3;

  OU ou_1 (.in_1(in_1), .in_2(in_2), .out_3(ou_1_out_3));
  OU ou_2 (.in_1(ou_1_out_3), .in_2(in_3), .out_3(ou_2_out_3));
  OU ou_3 (.in_1(ou_2_out_3), .in_2(in_4), .out_3(ou_3_out_3));
  OU ou_4 (.in_1(ou_3_out_3), .in_2(in_5), .out_3(ou_4_out_3));
  OU ou_5 (.in_1(ou_4_out_3), .in_2(in_6), .out_3(ou_5_out_3));
  OU ou_6 (.in_1(ou_5_out_3), .in_2(in_7), .out_3(out_8));
endmodule
