// Logisim project multiplicadorAGORAVAI.circ as structural Verilog: 1 circuit, main circuit main
module main (
  input  [7:0] in_1,
  input  [7:0] in_2
);

  wire clock_1_out, comparator_1_eq, not_1_out;
  wire [7:0] counter_1_q;
  wire [15:0] adder_1_out, register_1_q;

  Counter counter_1 (.Q(counter_1_q), .clk(clock_1_out));  // open: load, D, count, carry, clr
  Clock clock_1 (.out(clock_1_out));
  Comparator comparator_1 (.a(in_2), .b(counter_1_q), .eq(comparator_1_eq));  // open: gt, lt
  not not_1 (not_1_out, comparator_1_eq);
  Register #(.width(16)) register_1 (
    .D(adder_1_out), .en(not_1_out), .Q(register_1_q), .clk(clock_1_out));  // open: clr
  Adder adder_1 (.a(in_1), .b(register_1_q[7:0]), .out(adder_1_out[7:0]));  // open: cin, cout
  // Pins of 8 and 16 bits meet at adder_1_out
  // also tied to GND on the sheet: {register_1_q[8], register_1_q[9], register_1_q[10], register_1_q[11], register_1_q[12], register_1_q[13], register_1_q[14], register_1_q[15]}
endmodule
