// Logisim project multiplicasenhor.circ as structural Verilog: 1 circuit, main circuit main
module main (
  input  [15:0] A,
  input  RESET,
  input  [7:0] B
);

  wire clock_1_out, comparator_1_eq, not_1_out;
  wire [7:0] Contador_q;
  wire [15:0] adder_1_out, Registrador_q;

  Adder #(.width(16)) adder_1 (.a(A), .b(Registrador_q), .out(adder_1_out));  // open: cin, cout
  Register #(.width(16)) Registrador (
    .D(adder_1_out), .en(not_1_out), .Q(Registrador_q), .clk(clock_1_out), .clr(RESET));
  Counter Contador (.Q(Contador_q), .clk(clock_1_out), .clr(RESET));  // open: load, D, count, carry
  Clock clock_1 (.out(clock_1_out));
  // AND_Gate and_1 is placed but not wired
  Comparator comparator_1 (.a(Contador_q), .b(B), .eq(comparator_1_eq));  // open: gt, lt
  not not_1 (not_1_out, comparator_1_eq);
endmodule
