// Logisim project multiplierTESTE.circ as structural Verilog: 1 circuit, main circuit main
module main (
  input  [7:0] in_1,
  input  [7:0] in_2,
  output [15:0] out_3
);

  wire clock_1_out;
  wire [7:0] adder_1_out, and_1_out, register_1_q;

  assign and_1_out = in_1 & in_2;  // AND_Gate and_1, 8 bits wide
  Adder adder_1 (.a(and_1_out), .b(register_1_q), .out(adder_1_out));  // open: cin, cout
  Register register_1 (.D(adder_1_out), .Q(register_1_q), .clk(clock_1_out));  // open: en, clr
  Clock clock_1 (.out(clock_1_out));
endmodule
