// Logisim project multiplierTESTE2.circ as structural Verilog: 1 circuit, main circuit main
module main (
  input  in_1,
  input  [7:0] in_2,
  output out_3
);

  wire clock_1_out;
  wire [7:0] adder_1_out, register_1_q;

  Register register_1 (.D(adder_1_out), .Q(register_1_q), .clk(clock_1_out));  // open: en, clr
  Clock clock_1 (.out(clock_1_out));
  Adder adder_1 (.a(register_1_q), .b(in_2), .out(adder_1_out), .cin(in_1), .cout(out_3));
endmodule
