// Logisim project pipelining.circ as structural Verilog: 1 circuit, main circuit main
module main (
  input  [7:0] in_1
);

  wire clock_1_out;
  wire [7:0] adder_1_out, multiplier_1_out, register_1_q, register_2_q;

  Register register_1 (.Q(register_1_q));  // open: D, en, clk, clr
  Register register_2 (.Q(register_2_q));  // open: D, en, clk, clr
  Clock clock_1 (.out(clock_1_out));
  Multiplier multiplier_1 (.a(register_1_q), .b(register_2_q), .out(multiplier_1_out));  // open: cin, cout
  Adder adder_1 (.a(multiplier_1_out), .b(in_1), .out(adder_1_out));  // open: cin, cout
  Register register_3 (.D(adder_1_out), .Q(in_1), .clk(clock_1_out));  // open: en, clr
endmodule
