// Logisim project semaforo.circ as structural Verilog: 1 circuit, main circuit main
module main (
);

  wire and_1_out, and_2_out, and_3_out, clock_1_out, not_1_out, not_2_out, not_3_out, not_4_out, not_5_out,
       not_6_out, not_7_out, not_8_out, or_2_out, t_ff_1_q, t_ff_2_q, t_ff_3_q, t_ff_4_q, t_ff_5_q, t_ff_6_q,
       t_ff_7_q, t_ff_8_q;

  Clock clock_1 (.out(clock_1_out));
  T_Flip_Flop t_ff_1 (.clk(clock_1_out), .T(1'b1), .Q(t_ff_1_q), .reset(or_2_out));  // open: Qn, preset, en
  T_Flip_Flop t_ff_2 (.clk(t_ff_1_q), .T(1'b1), .Q(t_ff_2_q), .reset(or_2_out));  // open: Qn, preset, en
  and and_1 (and_1_out, t_ff_8_q, t_ff_6_q, t_ff_5_q, t_ff_4_q, not_1_out, not_2_out, not_3_out);
  not not_1 (not_1_out, t_ff_3_q);
  not not_2 (not_2_out, t_ff_2_q);
  not not_3 (not_3_out, t_ff_1_q);
  and and_2 (and_2_out, t_ff_8_q, t_ff_6_q, t_ff_5_q, not_4_out, not_5_out, t_ff_2_q, t_ff_1_q);
  not not_4 (not_4_out, t_ff_4_q);
  not not_5 (not_5_out, t_ff_3_q);
  not not_6 (not_6_out, t_ff_8_q);
  and and_3 (and_3_out, not_6_out, t_ff_6_q, t_ff_5_q, t_ff_4_q, t_ff_3_q, not_7_out, not_8_out);
  not not_7 (not_7_out, t_ff_2_q);
  not not_8 (not_8_out, t_ff_1_q);
  T_Flip_Flop t_ff_3 (.clk(t_ff_2_q), .T(1'b1), .Q(t_ff_3_q), .reset(or_2_out));  // open: Qn, preset, en
  T_Flip_Flop t_ff_4 (.clk(t_ff_3_q), .T(1'b1), .Q(t_ff_4_q), .reset(or_2_out));  // open: Qn, preset, en
  // OR_Gate or_1 has open pins: in0=and_1_out, in1=and_2_out, in2=and_3_out, out=open
  T_Flip_Flop t_ff_5 (.clk(t_ff_4_q), .T(1'b1), .Q(t_ff_5_q), .reset(or_2_out));  // open: Qn, preset, en
  T_Flip_Flop t_ff_6 (.clk(t_ff_5_q), .T(1'b1), .Q(t_ff_6_q), .reset(or_2_out));  // open: Qn, preset, en
  T_Flip_Flop t_ff_7 (.T(1'b1), .Q(t_ff_7_q), .reset(or_2_out));  // open: clk, Qn, preset, en
  T_Flip_Flop t_ff_8 (.clk(t_ff_6_q), .T(1'b1), .Q(t_ff_8_q), .reset(or_2_out));  // open: Qn, preset, en
  buf or_2 (or_2_out, and_1_out);  // OR_Gate
  T_Flip_Flop t_ff_9 (.clk(t_ff_7_q), .T(1'b1), .reset(or_2_out));  // open: Q, Qn, preset, en
endmodule
